// Logisim project cpu.circ as structural Verilog: 6 circuits, main circuit cpu
module Control_Unit (
  input  [3:0] op,
  output RegDst,
  output RegWrite,
  output MemRead,
  output MemToReg,
  output MemWrite,
  output ALUSrc,
  output Jump,
  output BNE,
  output BEQ,
  output ALUOp,
  output JAL,
  output LUI
);

  wire decoder_1_out0, decoder_1_out1, decoder_1_out2, decoder_1_out3, decoder_1_out12;

  Decoder #(.select(4), .enable("false")) decoder_1 (
    .out0(decoder_1_out0), .out1(decoder_1_out1), .out2(decoder_1_out2), .out3(decoder_1_out3),
    .out6(MemRead), .out7(MemWrite), .out10(BEQ), .out11(BNE), .out12(decoder_1_out12), .out13(JAL),
    .out15(LUI), .sel(op));  // open: out4, out5, out8, out9, out14
  or or_1 (RegDst, decoder_1_out0, decoder_1_out1, decoder_1_out2, decoder_1_out3);
  nor nor_1 (RegWrite, MemWrite, BEQ, BNE, decoder_1_out12);
  nor nor_2 (ALUSrc, RegDst, BEQ, BNE);
  or or_2 (Jump, decoder_1_out12, JAL);
  nor nor_3 (ALUOp, LUI, JAL, decoder_1_out12);

  assign MemToReg = MemRead;
endmodule

module Register_File (
  input  [15:0] WriteData,
  input  [2:0] R1,
  input  [2:0] R2,
  input  RegWrite,
  input  CLK,
  input  [2:0] Write_Register,
  output [15:0] Read_Data1,
  output [15:0] Read_Data2
);

  wire and_1_out, and_2_out, and_3_out, and_4_out, and_5_out, and_6_out, and_7_out, and_8_out,
       decoder_1_out0, decoder_1_out1, decoder_1_out2, decoder_1_out3, decoder_1_out4, decoder_1_out5,
       decoder_1_out6, decoder_1_out7, not_1_out;
  wire [15:0] register_1_q, register_2_q, register_3_q, register_4_q, register_5_q, register_6_q,
       register_7_q, register_8_q;

  Register #(.width(16)) register_1 (.D(WriteData), .en(and_1_out), .Q(register_1_q), .clk(CLK), .clr(not_1_out));
  and and_1 (and_1_out, RegWrite, decoder_1_out0);
  not not_1 (not_1_out, 1'b0);
  Register #(.width(16)) register_2 (.D(WriteData), .en(and_2_out), .Q(register_2_q), .clk(CLK), .clr(1'b0));
  and and_2 (and_2_out, RegWrite, decoder_1_out1);
  Register #(.width(16)) register_3 (.D(WriteData), .en(and_3_out), .Q(register_3_q), .clk(CLK), .clr(1'b0));
  and and_3 (and_3_out, RegWrite, decoder_1_out2);
  Register #(.width(16)) register_4 (.D(WriteData), .en(and_4_out), .Q(register_4_q), .clk(CLK), .clr(1'b0));
  and and_4 (and_4_out, RegWrite, decoder_1_out3);
  Decoder #(.select(3)) decoder_1 (
    .out0(decoder_1_out0), .out1(decoder_1_out1), .out2(decoder_1_out2), .out3(decoder_1_out3),
    .out4(decoder_1_out4), .out5(decoder_1_out5), .out6(decoder_1_out6), .out7(decoder_1_out7),
    .sel(Write_Register));  // open: en
  and and_5 (and_5_out, RegWrite, decoder_1_out4);
  and and_6 (and_6_out, RegWrite, decoder_1_out5);
  and and_7 (and_7_out, RegWrite, decoder_1_out6);
  and and_8 (and_8_out, RegWrite, decoder_1_out7);
  Register #(.width(16)) register_5 (.D(WriteData), .en(and_5_out), .Q(register_5_q), .clk(CLK), .clr(1'b0));
  Register #(.width(16)) register_6 (.D(WriteData), .en(and_6_out), .Q(register_6_q), .clk(CLK), .clr(1'b0));
  Register #(.width(16)) register_7 (.D(WriteData), .en(and_7_out), .Q(register_7_q), .clk(CLK), .clr(1'b0));
  Register #(.width(16)) register_8 (.D(WriteData), .en(and_8_out), .Q(register_8_q), .clk(CLK), .clr(1'b0));
  Multiplexer #(.select(3), .width(16)) multiplexer_1 (
    .in0(register_1_q), .in1(register_2_q), .in2(register_3_q), .in3(register_4_q), .in4(register_5_q),
    .in5(register_6_q), .in6(register_7_q), .in7(register_8_q), .out(Read_Data1), .sel(R1));  // open: en
  Multiplexer #(.select(3), .width(16)) multiplexer_2 (
    .in0(register_1_q), .in1(register_2_q), .in2(register_3_q), .in3(register_4_q), .in4(register_5_q),
    .in5(register_6_q), .in6(register_7_q), .in7(register_8_q), .out(Read_Data2), .sel(R2));  // open: en
endmodule

module ALU (
  input  ALUop,
  input  [15:0] Rs,
  input  [2:0] FUNC,
  input  [15:0] Rt,
  output [15:0] Result,
  output Zero
);

  wire comparator_1_lt;
  wire [15:0] adder_1_out, and_1_out, bitselector_1_out, nor_1_out, or_1_out, subtractor_1_out, xor_1_out;

  assign and_1_out = Rs & Rt;  // AND_Gate and_1, 16 bits wide
  assign or_1_out = Rs | Rt;  // OR_Gate or_1, 16 bits wide
  assign nor_1_out = ~(Rs | Rt);  // NOR_Gate nor_1, 16 bits wide
  assign xor_1_out = Rs ^ Rt;  // XOR_Gate xor_1, 16 bits wide
  Adder #(.width(16)) adder_1 (.a(Rs), .b(Rt), .out(adder_1_out));  // open: cin, cout
  Subtractor #(.width(16)) subtractor_1 (.a(Rs), .b(Rt), .out(subtractor_1_out));  // open: bin, bout
  Comparator #(.width(16)) comparator_1 (.a(Rs), .b(Rt), .eq(Zero), .lt(comparator_1_lt));  // open: gt
  Multiplexer #(.select(3), .width(16)) multiplexer_1 (
    .in0(and_1_out), .in1(or_1_out), .in2(nor_1_out), .in3(xor_1_out), .in4(adder_1_out),
    .in5(bitselector_1_out), .in6(subtractor_1_out), .in7(Rs), .out(Result), .sel(FUNC), .en(ALUop));
  BitSelector #(.width(1), .group(16)) bitselector_1 (.in(comparator_1_lt), .out(bitselector_1_out), .sel(1'b0));
endmodule

module cpu (
);

  wire alu_1_zero, and_1_out, and_2_out, and_3_out, clock_1_out, control_unit_1_aluop, control_unit_1_beq,
       control_unit_1_bne, control_unit_1_jump, control_unit_1_memread, control_unit_1_memtoreg,
       control_unit_1_memwrite, control_unit_1_regdst, control_unit_1_regwrite, or_2_out;
  wire [1:0] control_unit_1_jal, or_1_out;
  wire [2:0] multiplexer_1_out, multiplexer_2_out, multiplexer_3_out, multiplexer_6_out;
  wire [5:0] ram_1_data, ram_1_data_2;
  wire [11:0] adder_2_out;
  wire [15:0] adder_1_out, alu_1_result, bit_extender_1_out, bit_extender_2_out, bit_extender_3_out,
       data_mem_1_output, multiplexer_4_out, multiplexer_5_out, multiplexer_7_out, multiplexer_8_out,
       multiplexer_9_out, multiplexer_10_out, PC_q, register_file_1_read_data1, register_file_1_read_data2,
       shifter_1_out;
  wire [15:12] ram_1_data_3;

  Clock clock_1 (.out(clock_1_out));
  Register #(.width(16)) PC (.D(multiplexer_9_out), .Q(PC_q), .clk(clock_1_out));  // open: en, clr
  Adder #(.width(16)) adder_1 (.a(PC_q), .b(16'h1), .out(adder_1_out));  // open: cin, cout
  RAM #(.addrWidth(16), .dataWidth(16)) ram_1 (
    .addr(PC_q), .data({ram_1_data_3, ram_1_data_2, ram_1_data}), .sel(1'b1), .clk(clock_1_out), .ld(1'b1),
    .clr(1'b0));
  Adder #(.width(12)) adder_2 (.a({ram_1_data_2, ram_1_data}), .b(PC_q[11:0]), .out(adder_2_out));  // open: cin, cout
  assign bit_extender_1_out = {{4{1'b0}}, {ram_1_data_2, ram_1_data}};  // Bit_Extender bit_extender_1
  Multiplexer #(.width(3), .enable("false")) multiplexer_1 (
    .in0(ram_1_data_2[2:0]), .in1(ram_1_data[5:3]), .out(multiplexer_1_out), .sel(control_unit_1_regdst));
  assign bit_extender_2_out = {{10{ram_1_data[5]}}, ram_1_data};  // Bit_Extender bit_extender_2
  Shifter #(.width(16)) shifter_1 (.in(bit_extender_1_out), .\dist (4'b0100), .out(shifter_1_out));
  Multiplexer #(.width(3), .enable("false")) multiplexer_2 (
    .in0(multiplexer_1_out), .in1(3'b111), .out(multiplexer_2_out), .sel(control_unit_1_jal[0]));
  Multiplexer #(.width(3), .enable("false")) multiplexer_3 (
    .in0(multiplexer_2_out), .in1(3'b001), .out(multiplexer_3_out), .sel(control_unit_1_jal[1]));
  Register_File register_file_1 (
    .WriteData(multiplexer_4_out), .RegWrite(control_unit_1_regwrite), .CLK(clock_1_out),
    .Write_Register(multiplexer_3_out), .Read_Data1(register_file_1_read_data1),
    .Read_Data2(register_file_1_read_data2), .R1(ram_1_data_2[5:3]), .R2(ram_1_data_2[2:0]));
  Multiplexer #(.select(2), .width(16), .enable("false")) multiplexer_4 (
    .in0(multiplexer_10_out), .in1(adder_1_out), .in2(shifter_1_out), .out(multiplexer_4_out),
    .sel(control_unit_1_jal));  // open: in3
  Control_Unit control_unit_1 (
    .op(ram_1_data_3), .RegDst(control_unit_1_regdst), .RegWrite(control_unit_1_regwrite),
    .MemRead(control_unit_1_memread), .MemToReg(control_unit_1_memtoreg), .MemWrite(control_unit_1_memwrite),
    .ALUSrc(or_1_out[1]), .Jump(control_unit_1_jump), .BNE(control_unit_1_bne), .ALUOp(control_unit_1_aluop),
    .JAL(control_unit_1_jal[0]), .LUI(control_unit_1_jal[1]), .BEQ(control_unit_1_beq));
  Multiplexer #(.width(16), .enable("false")) multiplexer_5 (
    .in0(register_file_1_read_data2), .in1(bit_extender_2_out), .out(multiplexer_5_out), .sel(or_1_out[1]));
  or or_1 (or_1_out[0], control_unit_1_memread, control_unit_1_memwrite);
  Multiplexer #(.select(2), .width(3), .enable("false")) multiplexer_6 (
    .in0(ram_1_data[2:0]), .in1(3'b100), .in2(ram_1_data_3[14:12]), .in3(3'b100), .out(multiplexer_6_out),
    .sel(or_1_out));
  assign bit_extender_3_out = {{10{1'b0}}, ram_1_data};  // Bit_Extender bit_extender_3
  ALU alu_1 (
    .Rs(register_file_1_read_data1), .Rt(multiplexer_5_out), .ALUop(control_unit_1_aluop),
    .FUNC(multiplexer_6_out), .Zero(alu_1_zero), .Result(alu_1_result));
  Multiplexer #(.width(16), .enable("false")) multiplexer_7 (
    .in0(adder_1_out), .in1(bit_extender_3_out), .out(multiplexer_7_out), .sel(or_2_out));
  or or_2 (or_2_out, and_1_out, and_2_out);
  and and_1 (and_1_out, alu_1_zero, control_unit_1_beq);
  and and_2 (and_2_out, control_unit_1_bne, ~alu_1_zero);  // AND_Gate
  Multiplexer #(.width(16), .enable("false")) multiplexer_8 (
    .in0(multiplexer_7_out), .in1({adder_1_out[15:12], adder_2_out}), .out(multiplexer_8_out),
    .sel(control_unit_1_jump));
  and and_3 (and_3_out, control_unit_1_aluop, multiplexer_6_out[2], ~or_2_out, multiplexer_6_out[1], multiplexer_6_out[0]);  // AND_Gate
  Multiplexer #(.width(16), .enable("false")) multiplexer_9 (
    .in0(multiplexer_8_out), .in1(alu_1_result), .out(multiplexer_9_out), .sel(and_3_out));
  Multiplexer #(.width(16), .enable("false")) multiplexer_10 (
    .in0(alu_1_result), .in1(data_mem_1_output), .out(multiplexer_10_out), .sel(control_unit_1_memtoreg));
  Data_Mem data_mem_1 (
    .Address(alu_1_result), .MemRead(control_unit_1_memread), .MemWrite(control_unit_1_memwrite),
    .WriteData(register_file_1_read_data2), .Output(data_mem_1_output), .CLK(clock_1_out));
endmodule

module Data_Mem (
  input  [15:0] Address,
  input  MemRead,
  input  CLK,
  input  MemWrite,
  input  [15:0] WriteData,
  output [15:0] Output
);

  wire not_1_out, xor_1_out;

  xor xor_1 (xor_1_out, MemRead, MemWrite);
  RAM #(.addrWidth(16), .dataWidth(16)) ram_1 (
    .addr(Address), .data(Output), .sel(xor_1_out), .clk(CLK), .ld(not_1_out), .clr(1'b0));
  not not_1 (not_1_out, MemWrite);
  assign Output = MemWrite ? WriteData : 16'bz;  // Controlled_Buffer controlled_buffer_1
endmodule

module ALUCtrl (
  input  [2:0] R_TYPE,
  input  [2:0] I_TYPE
);

  Multiplexer #(.select(2)) multiplexer_1 ();  // open: in0, in1, in2, in3, out, sel, en
endmodule
